// Logisim project vpu.circ as structural Verilog: 10 circuits, main circuit VPU
module VPU (
  input  clk,
  input  Ex,
  input  [5:0] vop,
  input  [4:0] vrd,
  input  [4:0] vrs,
  input  [31:0] RamOutHi,
  input  [31:0] RamOutLo,
  input  [23:0] RegOut,
  output VBus32,
  output VBus64,
  output [31:0] VRegOutHi,
  output [31:0] VRegOutLo,
  output VPUError
);

  wire BusEn, cfg, PackIn, PackOut, WEn;
  wire [2:0] ALUop, DataSrc;
  wire [31:0] ALUOutHi, ALUOutLo, InHi, InLo, vrsOutHi, vrsOutLo;
  wire [31:16] ImmS, ImmZ;

  assign ImmS = {{11{vrs[4]}}, vrs};  // Bit_Extender bit_extender_1
  assign ImmZ = {{11{1'b0}}, vrs};  // Bit_Extender bit_extender_2
  VRegCtrl vregctrl_1 (
    .vop(vop), .cfg(cfg), .WEn(WEn), .PackOut(PackOut), .PackIn(PackIn), .DataSrc(DataSrc), .ALUop(ALUop),
    .Ex(Ex), .BusEn(BusEn));
  Multiplexer #(.select(3), .width(32), .enable("false")) multiplexer_1 (
    .in0(RamOutHi), .in1({ImmS, ImmS}), .in2({ImmZ, ImmZ}), .in3({RegOut[15:0], RegOut[15:0]}),
    .in4(ALUOutHi), .in5(vrsOutHi), .out(InHi), .sel(DataSrc));  // open: in6, in7
  Multiplexer #(.select(3), .width(32), .enable("false")) multiplexer_2 (
    .in0(RamOutLo), .in1({ImmS, ImmS}), .in2({ImmZ, ImmZ}), .in3({RegOut[15:0], RegOut[15:0]}),
    .in4(ALUOutLo), .in5(vrsOutLo), .out(InLo), .sel(DataSrc));  // open: in6, in7
  VReg vreg_1 (
    .clk(clk), .InHi(InHi), .InLo(InLo), .WEn(WEn), .vrsOutHi(vrsOutHi), .vrsOutLo(vrsOutLo),
    .vrdOutHi(VRegOutHi), .vrdOutLo(VRegOutLo), .cfg(cfg), .vrd(vrd), .vrs(vrs), .PackIn(PackIn),
    .PackOut(PackOut), .VBus32(VBus32), .VBus64(VBus64), .BusEn(BusEn));
  VALU valu_1 (
    .AHi(VRegOutHi), .ALo(VRegOutLo), .op(ALUop), .BHi(vrsOutHi), .BLo(vrsOutLo), .ResHi(ALUOutHi),
    .ResLo(ALUOutLo));

  assign VPUError = 1'b0;

  // Other names for the same wires on the sheet: ImmS[15:0] = ImmS; ImmZ[15:0] = ImmZ;
  //   RegOutEx[31:0] = {RegOut[15:0], RegOut[15:0]}; vrdOutHi[31:0] = VRegOutHi; vrdOutLo[31:0] = VRegOutLo
endmodule

module VRegRow (
  input  [31:0] InHi,
  input  [31:0] InLo,
  input  [3:0] RegEn,
  input  clk,
  input  is16,
  input  RowEn,
  output [31:0] OutHi,
  output [31:0] OutLo
);

  wire [0:0] bitadder_1_out;
  wire [1:0] InSel;
  wire [3:0] and_1_out;
  wire [7:0] multiplexer_1_out, multiplexer_2_out, multiplexer_3_out, multiplexer_4_out, multiplexer_5_out,
       multiplexer_6_out;

  Register register_1 (.D(InHi[31:24]), .en(and_1_out[3]), .Q(OutHi[31:24]), .clk(clk));  // open: clr
  Register register_2 (.D(InHi[23:16]), .en(and_1_out[3]), .Q(OutHi[23:16]), .clk(clk));  // open: clr
  Multiplexer #(.select(2), .width(8), .enable("false")) multiplexer_1 (
    .in0(InHi[31:24]), .in1(InHi[15:8]), .in2(InHi[15:8]), .out(multiplexer_1_out), .sel(InSel));  // open: in3
  Multiplexer #(.select(2), .width(8), .enable("false")) multiplexer_2 (
    .in0(InHi[23:16]), .in1(InHi[7:0]), .in2(InHi[7:0]), .out(multiplexer_2_out), .sel(InSel));  // open: in3
  Register register_3 (.D(multiplexer_1_out), .en(and_1_out[2]), .Q(OutHi[15:8]), .clk(clk));  // open: clr
  Register register_4 (.D(multiplexer_2_out), .en(and_1_out[2]), .Q(OutHi[7:0]), .clk(clk));  // open: clr
  Multiplexer #(.select(2), .width(8), .enable("false")) multiplexer_3 (
    .in0(InHi[31:24]), .in1(InHi[31:24]), .in2(InLo[31:24]), .out(multiplexer_3_out), .sel(InSel));  // open: in3
  Multiplexer #(.select(2), .width(8), .enable("false")) multiplexer_4 (
    .in0(InHi[23:16]), .in1(InHi[23:16]), .in2(InLo[23:16]), .out(multiplexer_4_out), .sel(InSel));  // open: in3
  Register register_5 (.D(multiplexer_3_out), .en(and_1_out[1]), .Q(OutLo[31:24]), .clk(clk));  // open: clr
  Register register_6 (.D(multiplexer_4_out), .en(and_1_out[1]), .Q(OutLo[23:16]), .clk(clk));  // open: clr
  Multiplexer #(.select(2), .width(8), .enable("false")) multiplexer_5 (
    .in0(InHi[31:24]), .in1(InHi[15:8]), .in2(InLo[15:8]), .out(multiplexer_5_out), .sel(InSel));  // open: in3
  Multiplexer #(.select(2), .width(8), .enable("false")) multiplexer_6 (
    .in0(InHi[23:16]), .in1(InHi[7:0]), .in2(InLo[7:0]), .out(multiplexer_6_out), .sel(InSel));  // open: in3
  Register register_7 (.D(multiplexer_5_out), .en(and_1_out[0]), .Q(OutLo[15:8]), .clk(clk));  // open: clr
  Register register_8 (.D(multiplexer_6_out), .en(and_1_out[0]), .Q(OutLo[7:0]), .clk(clk));  // open: clr
  assign and_1_out = RegEn & {4{RowEn}};  // AND_Gate and_1, 4 bits wide
  BitAdder #(.width(4)) bitadder_1 (.in0(RegEn), .out({InSel, bitadder_1_out[0]}));

  // Other names for the same wires on the sheet: reg3[7:0] = OutHi[7:0]; reg2[7:0] = OutHi[15:8];
  //   reg1[7:0] = OutHi[23:16]; reg0[7:0] = OutHi[31:24]; reg7[7:0] = OutLo[7:0]; reg6[7:0] = OutLo[15:8];
  //   reg5[7:0] = OutLo[23:16]; reg4[7:0] = OutLo[31:24]
endmodule

module VReg (
  input  BusEn,
  input  [31:0] InHi,
  input  cfg,
  input  clk,
  input  [4:0] vrd,
  input  WEn,
  input  [4:0] vrs,
  input  [31:0] InLo,
  input  PackOut,
  input  PackIn,
  output [31:0] vrdOutHi,
  output [31:0] vrsOutHi,
  output [31:0] vrdOutLo,
  output [31:0] vrsOutLo,
  output VBus32,
  output VBus64
);

  wire and_1_out, and_2_out, demultiplexer_1_out0, demultiplexer_1_out1, demultiplexer_1_out2,
       demultiplexer_1_out3, demultiplexer_1_out4, demultiplexer_1_out5, demultiplexer_1_out6,
       demultiplexer_1_out7, demultiplexer_2_out0, demultiplexer_2_out1, demultiplexer_2_out2,
       demultiplexer_2_out3, demultiplexer_2_out4, demultiplexer_2_out5, demultiplexer_2_out6,
       demultiplexer_2_out7, not_1_out, not_2_out, not_3_out, vrd16, vrs16;
  wire [2:0] bitadder_1_out, vlen;
  wire [3:0] RegSel1, RegSel2, RowSel1, RowSel2;
  wire [4:0] num16;
  wire [31:0] InHi_t, InLo_t, pack_1_outhi, r00H, r00L, r01H, r01L, r02H, r02L, r03H, r03L, r04H, r04L, r05H,
       r05L, r06H, r06L, r07H, r07L, r08H, r08L, r09H, r09L, r10H, r10L, r11H, r11L, r12H, r12L, r13H, r13L,
       r14H, r14L, r15H, r15L, rOutHi1, rOutHi2, rOutLo1, rOutLo2;

  VRegRow vregrow_1 (
    .InHi(InHi_t), .InLo(InLo_t), .OutHi(r00H), .OutLo(r00L), .RowEn(demultiplexer_1_out0), .RegEn(RegSel1),
    .clk(clk), .is16(vrd16));
  VRegRow vregrow_2 (
    .InHi(InHi_t), .InLo(InLo_t), .OutHi(r01H), .OutLo(r01L), .RowEn(demultiplexer_1_out1), .RegEn(RegSel1),
    .clk(clk), .is16(vrd16));
  VRegRow vregrow_3 (
    .InHi(InHi_t), .InLo(InLo_t), .OutHi(r02H), .OutLo(r02L), .RowEn(demultiplexer_1_out2), .RegEn(RegSel1),
    .clk(clk), .is16(vrd16));
  VRegRow vregrow_4 (
    .InHi(InHi_t), .InLo(InLo_t), .OutHi(r03H), .OutLo(r03L), .RowEn(demultiplexer_1_out3), .RegEn(RegSel1),
    .clk(clk), .is16(vrd16));
  VRegRow vregrow_5 (
    .InHi(InHi_t), .InLo(InLo_t), .OutHi(r04H), .OutLo(r04L), .RowEn(demultiplexer_1_out4), .RegEn(RegSel1),
    .clk(clk), .is16(vrd16));
  VRegRow vregrow_6 (
    .InHi(InHi_t), .InLo(InLo_t), .OutHi(r05H), .OutLo(r05L), .RowEn(demultiplexer_1_out5), .RegEn(RegSel1),
    .clk(clk), .is16(vrd16));
  VRegRow vregrow_7 (
    .InHi(InHi_t), .InLo(InLo_t), .OutHi(r06H), .OutLo(r06L), .RowEn(demultiplexer_1_out6), .RegEn(RegSel1),
    .clk(clk), .is16(vrd16));
  VRegRow vregrow_8 (
    .InHi(InHi_t), .InLo(InLo_t), .OutHi(r07H), .OutLo(r07L), .RowEn(demultiplexer_1_out7), .RegEn(RegSel1),
    .clk(clk), .is16(vrd16));
  not not_1 (not_1_out, RowSel1[3]);
  Demultiplexer #(.select(3), .disabled(0)) demultiplexer_1 (
    .out0(demultiplexer_1_out0), .out1(demultiplexer_1_out1), .out2(demultiplexer_1_out2),
    .out3(demultiplexer_1_out3), .out4(demultiplexer_1_out4), .out5(demultiplexer_1_out5),
    .out6(demultiplexer_1_out6), .out7(demultiplexer_1_out7), .in(WEn), .sel(RowSel1[2:0]), .en(not_1_out));
  Register #(.width(5)) register_1 (.D(vrd), .en(cfg), .Q(num16), .clk(clk));  // open: clr
  Register #(.width(3)) register_2 (.D(vrs[2:0]), .en(cfg), .Q(vlen), .clk(clk));  // open: clr
  VRegRow vregrow_9 (
    .InHi(InHi_t), .InLo(InLo_t), .OutHi(r08H), .OutLo(r08L), .RowEn(demultiplexer_2_out0), .RegEn(RegSel1),
    .clk(clk), .is16(vrd16));
  VRegRow vregrow_10 (
    .InHi(InHi_t), .InLo(InLo_t), .OutHi(r09H), .OutLo(r09L), .RowEn(demultiplexer_2_out1), .RegEn(RegSel1),
    .clk(clk), .is16(vrd16));
  VRegRow vregrow_11 (
    .InHi(InHi_t), .InLo(InLo_t), .OutHi(r10H), .OutLo(r10L), .RowEn(demultiplexer_2_out2), .RegEn(RegSel1),
    .clk(clk), .is16(vrd16));
  VRegRow vregrow_12 (
    .InHi(InHi_t), .InLo(InLo_t), .OutHi(r11H), .OutLo(r11L), .RowEn(demultiplexer_2_out3), .RegEn(RegSel1),
    .clk(clk), .is16(vrd16));
  VRegRow vregrow_13 (
    .InHi(InHi_t), .InLo(InLo_t), .OutHi(r12H), .OutLo(r12L), .RowEn(demultiplexer_2_out4), .RegEn(RegSel1),
    .clk(clk), .is16(vrd16));
  VRegRow vregrow_14 (
    .InHi(InHi_t), .InLo(InLo_t), .OutHi(r13H), .OutLo(r13L), .RowEn(demultiplexer_2_out5), .RegEn(RegSel1),
    .clk(clk), .is16(vrd16));
  VRegRow vregrow_15 (
    .InHi(InHi_t), .InLo(InLo_t), .OutHi(r14H), .OutLo(r14L), .RowEn(demultiplexer_2_out6), .RegEn(RegSel1),
    .clk(clk), .is16(vrd16));
  VRegRow vregrow_16 (
    .InHi(InHi_t), .InLo(InLo_t), .OutHi(r15H), .OutLo(r15L), .RowEn(demultiplexer_2_out7), .RegEn(RegSel1),
    .clk(clk), .is16(vrd16));
  VTC vtc_1 (.vlen(vlen), .num16(num16), .VirtAddr(vrd), .VTCSel({RowSel1, RegSel1}), .is16(vrd16));
  Demultiplexer #(.select(3), .disabled(0)) demultiplexer_2 (
    .out0(demultiplexer_2_out0), .out1(demultiplexer_2_out1), .out2(demultiplexer_2_out2),
    .out3(demultiplexer_2_out3), .out4(demultiplexer_2_out4), .out5(demultiplexer_2_out5),
    .out6(demultiplexer_2_out6), .out7(demultiplexer_2_out7), .in(WEn), .sel(RowSel1[2:0]), .en(RowSel1[3]));
  VTC vtc_2 (.vlen(vlen), .num16(num16), .VirtAddr(vrs), .VTCSel({RowSel2, RegSel2}), .is16(vrs16));
  Multiplexer #(.select(4), .width(32), .enable("false")) multiplexer_1 (
    .in0(r00H), .in1(r01H), .in2(r02H), .in3(r03H), .in4(r04H), .in5(r05H), .in6(r06H), .in7(r07H),
    .in8(r08H), .in9(r09H), .in10(r10H), .in11(r11H), .in12(r12H), .in13(r13H), .in14(r14H), .in15(r15H),
    .out(rOutHi1), .sel(RowSel1));
  Multiplexer #(.select(4), .width(32), .enable("false")) multiplexer_2 (
    .in0(r00L), .in1(r01L), .in2(r02L), .in3(r03L), .in4(r04L), .in5(r05L), .in6(r06L), .in7(r07L),
    .in8(r08L), .in9(r09L), .in10(r10L), .in11(r11L), .in12(r12L), .in13(r13L), .in14(r14L), .in15(r15L),
    .out(rOutLo1), .sel(RowSel1));
  Pack pack_1 (.InHi(InHi), .InLo(InLo), .OutHi(pack_1_outhi));
  Multiplexer #(.width(32), .enable("false")) multiplexer_3 (
    .in0(InHi), .in1(pack_1_outhi), .out(InHi_t), .sel(and_1_out));
  and and_1 (and_1_out, PackIn, not_2_out);
  not not_2 (not_2_out, vrd16);
  Multiplexer #(.width(32), .enable("false")) multiplexer_4 (
    .in0(InLo), .in1({32{1'b0}}), .out(InLo_t), .sel(and_2_out));
  and and_2 (and_2_out, PackIn, not_3_out);
  not not_3 (not_3_out, vrd16);
  Multiplexer #(.select(4), .width(32), .enable("false")) multiplexer_5 (
    .in0(r00H), .in1(r01H), .in2(r02H), .in3(r03H), .in4(r04H), .in5(r05H), .in6(r06H), .in7(r07H),
    .in8(r08H), .in9(r09H), .in10(r10H), .in11(r11H), .in12(r12H), .in13(r13H), .in14(r14H), .in15(r15H),
    .out(rOutHi2), .sel(RowSel2));
  Multiplexer #(.select(4), .width(32), .enable("false")) multiplexer_6 (
    .in0(r00L), .in1(r01L), .in2(r02L), .in3(r03L), .in4(r04L), .in5(r05L), .in6(r06L), .in7(r07L),
    .in8(r08L), .in9(r09L), .in10(r10L), .in11(r11L), .in12(r12L), .in13(r13L), .in14(r14L), .in15(r15L),
    .out(rOutLo2), .sel(RowSel2));
  VOM vom_1 (
    .InHi(rOutHi1), .InLo(rOutLo1), .DSel(RegSel1), .is16(vrd16), .OutHi(vrdOutHi), .OutLo(vrdOutLo),
    .PackOut(PackOut));
  VOM vom_2 (
    .InHi(rOutHi2), .InLo(rOutLo2), .DSel(RegSel2), .is16(vrs16), .OutHi(vrsOutHi), .OutLo(vrsOutLo),
    .PackOut(PackOut));
  BitAdder #(.width(4)) bitadder_1 (.in0(RegSel1), .out(bitadder_1_out));
  and and_3 (VBus32, BusEn, bitadder_1_out[1]);
  and and_4 (VBus64, bitadder_1_out[2], BusEn);
endmodule

module VRegCtrl (
  input  [5:0] vop,
  input  Ex,
  output cfg,
  output PackOut,
  output BusEn,
  output WEn,
  output PackIn,
  output [2:0] DataSrc,
  output [2:0] ALUop
);

  wire comparator_16_eq, lv, lvi, lviu, lvr, vadd, vALU, vb2ws, vb2wz, vdiv, vmov, vmul, vsub, vw2bh, vw2bl;
  wire [5:0] multiplexer_1_out;

  Multiplexer #(.width(6), .enable("false")) multiplexer_1 (
    .in0({6{1'b0}}), .in1(vop), .out(multiplexer_1_out), .sel(Ex));
  Comparator #(.width(6), .mode("unsigned")) comparator_1 (
    .a(multiplexer_1_out), .b(6'b100000), .eq(cfg));  // open: gt, lt
  Comparator #(.width(6), .mode("unsigned")) comparator_2 (
    .a(multiplexer_1_out), .b(6'b100001), .eq(lv));  // open: gt, lt
  Comparator #(.width(6), .mode("unsigned")) comparator_3 (
    .a(multiplexer_1_out), .b(6'b100010), .eq(BusEn));  // open: gt, lt
  Comparator #(.width(6), .mode("unsigned")) comparator_4 (
    .a(multiplexer_1_out), .b(6'b100011), .eq(lvi));  // open: gt, lt
  Comparator #(.width(6), .mode("unsigned")) comparator_5 (
    .a(multiplexer_1_out), .b(6'b100100), .eq(lviu));  // open: gt, lt
  Comparator #(.width(6), .mode("unsigned")) comparator_6 (
    .a(multiplexer_1_out), .b(6'b100101), .eq(lvr));  // open: gt, lt
  Comparator #(.width(6), .mode("unsigned")) comparator_7 (
    .a(multiplexer_1_out), .b(6'b100110), .eq(vw2bh));  // open: gt, lt
  Comparator #(.width(6), .mode("unsigned")) comparator_8 (
    .a(multiplexer_1_out), .b(6'b100111), .eq(vw2bl));  // open: gt, lt
  Comparator #(.width(6), .mode("unsigned")) comparator_9 (
    .a(multiplexer_1_out), .b(6'b101000), .eq(vb2ws));  // open: gt, lt
  Comparator #(.width(6), .mode("unsigned")) comparator_10 (
    .a(multiplexer_1_out), .b(6'b101001), .eq(vb2wz));  // open: gt, lt
  Comparator #(.width(6), .mode("unsigned")) comparator_11 (
    .a(multiplexer_1_out), .b(6'b101010), .eq(vmov));  // open: gt, lt
  Comparator #(.width(6), .mode("unsigned")) comparator_12 (
    .a(multiplexer_1_out), .b(6'b101011), .eq(vadd));  // open: gt, lt
  Comparator #(.width(6), .mode("unsigned")) comparator_13 (
    .a(multiplexer_1_out), .b(6'b101100), .eq(vsub));  // open: gt, lt
  Comparator #(.width(6), .mode("unsigned")) comparator_14 (
    .a(multiplexer_1_out), .b(6'b101101), .eq(vmul));  // open: gt, lt
  Comparator #(.width(6), .mode("unsigned")) comparator_15 (
    .a(multiplexer_1_out), .b(6'b101110), .eq(vdiv));  // open: gt, lt
  Comparator #(.width(6), .mode("unsigned")) comparator_16 (
    .a(multiplexer_1_out), .b(6'b101111), .eq(comparator_16_eq));  // open: gt, lt
  or or_1 (vALU, vw2bh, vw2bl, vb2ws, vb2wz, vadd, vsub, vmul, vdiv);
  or or_2 (WEn, lv, lvi, lviu, lvr, vALU, vmov);
  or or_3 (PackIn, vALU, lvi, vmov, lviu, lvr);
  or or_4 (DataSrc[2], vmov, vALU);
  or or_5 (DataSrc[1], lviu, lvr);
  or or_6 (DataSrc[0], lvi, vmov, lvr);
  or or_7 (ALUop[2], vw2bh, vw2bl, vb2ws, vb2wz);
  or or_8 (ALUop[1], vmul, vdiv, vb2ws, vb2wz);
  or or_9 (ALUop[0], vsub, vdiv, vw2bl, vb2wz);

  assign PackOut = BusEn;

  // Other names for the same wires on the sheet: sv = BusEn; vcfg = cfg

  // Notes on the sheet:
  //   vcfg
  //   lv
  //   sv
  //   lvi
  //   lviu
  //   lvr
  //   vw2bh
  //   vw2bl
  //   vb2ws
  //   vb2wz
  //   vmov
  //   vadd
  //   vsub
  //   vmul
  //   vdiv
  //   UNUSED
endmodule

module VTC (
  input  [2:0] vlen,
  input  [4:0] num16,
  input  [4:0] VirtAddr,
  output [7:0] VTCSel,
  output is16
);

  wire islen4, not_1_out;
  wire [1:0] bit_extender_4_out, bit_extender_5_out, priority_encoder_1_out, RegSel;
  wire [2:0] lgvlen;
  wire [3:0] adder_2_out, adder_3_out, demultiplexer_1_out0, shifter_1_out, shifter_2_out;
  wire [7:0] adder_1_out, bit_extender_1_out, multiplexer_1_out, shifter_3_out, shifter_4_out, shifter_5_out,
       vaddr;

  Demultiplexer #(.select(2), .enable("false")) demultiplexer_1 (
    .out0(demultiplexer_1_out0[0]), .out1(demultiplexer_1_out0[1]), .out2(demultiplexer_1_out0[2]),
    .out3(demultiplexer_1_out0[3]), .in(1'b1), .sel(RegSel));
  assign bit_extender_1_out = {{3{1'b0}}, num16};  // Bit_Extender bit_extender_1
  assign {lgvlen[2], islen4, lgvlen[0]} = {{1{1'b0}}, priority_encoder_1_out};  // Bit_Extender bit_extender_2
  Priority_Encoder #(.select(2), .disabled(0)) priority_encoder_1 (
    .in0(vlen[0]), .in1(vlen[1]), .in2(vlen[2]), .out(priority_encoder_1_out));  // open: in3, gs, en_out, en_in
  assign vaddr = {{3{1'b0}}, VirtAddr};  // Bit_Extender bit_extender_3
  assign bit_extender_4_out = {{1{1'b0}}, islen4};  // Bit_Extender bit_extender_4
  assign bit_extender_5_out = {{1{1'b0}}, is16};  // Bit_Extender bit_extender_5
  Adder adder_1 (.a(bit_extender_1_out), .b(vaddr), .out(adder_1_out));  // open: cin, cout
  Comparator comparator_1 (.a(vaddr), .b(bit_extender_1_out), .lt(is16));  // open: gt, eq
  Shifter #(.width(4)) shifter_1 (.in(demultiplexer_1_out0), .\dist (bit_extender_4_out), .out(shifter_1_out));
  Shifter #(.width(4)) shifter_2 (.in(demultiplexer_1_out0), .\dist (bit_extender_5_out), .out(shifter_2_out));
  Shifter shifter_3 (.in(vaddr), .\dist ({lgvlen[2], islen4, lgvlen[0]}), .out(shifter_3_out));
  Adder #(.width(4)) adder_2 (.a(demultiplexer_1_out0), .b(shifter_1_out), .out(adder_2_out));  // open: cin, cout
  Adder #(.width(4)) adder_3 (.a(demultiplexer_1_out0), .b(shifter_2_out), .out(adder_3_out));  // open: cin, cout
  Shifter shifter_4 (.in(shifter_3_out), .\dist (3'b001), .out(shifter_4_out));
  // Probe on {multiplexer_1_out[7], VTCSel[7:4], RegSel, multiplexer_1_out[0]}
  Multiplexer #(.width(8), .enable("false")) multiplexer_1 (
    .in0(shifter_4_out), .in1(shifter_5_out),
    .out({multiplexer_1_out[7], VTCSel[7:4], RegSel, multiplexer_1_out[0]}), .sel(not_1_out));
  Shifter shifter_5 (.in(adder_1_out), .\dist ({lgvlen[2], islen4, lgvlen[0]}), .out(shifter_5_out));
  not not_1 (not_1_out, is16);
  Multiplexer #(.select(2), .width(4), .enable("false")) multiplexer_2 (
    .in0(demultiplexer_1_out0), .in1(adder_2_out), .in2(adder_3_out), .in3(4'b1111), .out(VTCSel[3:0]),
    .sel({is16, islen4}));

  // Other names for the same wires on the sheet: lgvlen[1] = islen4; RowSel[3:0] = VTCSel[7:4]

  // Notes on the sheet:
  //   PA - 4 MSB - RowSel
  //   PA - 4 LSB - RegSetSel
endmodule

module VOM (
  input  [31:0] InHi,
  input  [31:0] InLo,
  input  [3:0] DSel,
  input  is16,
  input  PackOut,
  output [31:0] OutHi,
  output [31:0] OutLo
);

  wire Lo2Hi, nor_2_out, nor_3_out, shift, xor_1_out;
  wire [15:0] bit_extender_1_out, bit_extender_2_out, bit_extender_3_out, bit_extender_4_out, MaskHi0,
       MaskHi16, MaskLo0, MaskLo16, multiplexer_2_out, multiplexer_3_out;
  wire [31:0] PackedHi, PackedLo, shifter_1_out, UnpackedHi, UnpackedLo;

  Multiplexer #(.disabled(0)) multiplexer_1 (.in0(DSel[2]), .in1(DSel[0]), .out(shift), .sel(Lo2Hi), .en(xor_1_out));
  assign bit_extender_1_out = {{15{DSel[3]}}, DSel[3]};  // Bit_Extender bit_extender_1
  assign bit_extender_2_out = {{15{DSel[2]}}, DSel[2]};  // Bit_Extender bit_extender_2
  assign bit_extender_3_out = {{15{DSel[1]}}, DSel[1]};  // Bit_Extender bit_extender_3
  assign bit_extender_4_out = {{15{DSel[0]}}, DSel[0]};  // Bit_Extender bit_extender_4
  nor nor_1 (Lo2Hi, DSel[3], DSel[2]);
  xor xor_1 (xor_1_out, DSel[3], DSel[2], DSel[1], DSel[0]);
  assign MaskHi16 = bit_extender_1_out & InHi[31:16];  // AND_Gate and_1, 16 bits wide
  assign MaskHi0 = bit_extender_2_out & InHi[15:0];  // AND_Gate and_2, 16 bits wide
  assign MaskLo16 = bit_extender_3_out & InLo[31:16];  // AND_Gate and_3, 16 bits wide
  assign MaskLo0 = bit_extender_4_out & InLo[15:0];  // AND_Gate and_4, 16 bits wide
  Multiplexer #(.width(16), .enable("false")) multiplexer_2 (
    .in0(MaskHi16), .in1(MaskLo16), .out(multiplexer_2_out), .sel(Lo2Hi));
  Multiplexer #(.width(16), .enable("false")) multiplexer_3 (
    .in0(MaskHi0), .in1(MaskLo0), .out(multiplexer_3_out), .sel(Lo2Hi));
  Shifter #(.width(32)) shifter_1 (.in({multiplexer_2_out, multiplexer_3_out}), .\dist (5'b10000), .out(shifter_1_out));
  // Probe on PackedHi
  Multiplexer #(.width(32), .enable("false")) multiplexer_4 (
    .in0({multiplexer_2_out, multiplexer_3_out}), .in1(shifter_1_out), .out(PackedHi), .sel(shift));
  UnPack unpack_1 (.OutHi(UnpackedHi), .OutLo(UnpackedLo), .In(PackedHi));
  Multiplexer #(.width(32), .enable("false")) multiplexer_5 (
    .in0({MaskLo16, MaskLo0}), .in1({32{1'b0}}), .out(PackedLo), .sel(Lo2Hi));
  // Probe on PackedLo
  Multiplexer #(.width(32), .enable("false")) multiplexer_6 (
    .in0(PackedHi), .in1(UnpackedHi), .out(OutHi), .sel(nor_2_out));
  nor nor_2 (nor_2_out, is16, PackOut);
  Multiplexer #(.width(32), .enable("false")) multiplexer_7 (
    .in0(PackedLo), .in1(UnpackedLo), .out(OutLo), .sel(nor_3_out));
  nor nor_3 (nor_3_out, is16, PackOut);

  // Other names for the same wires on the sheet: DSel4[3:0] = DSel; InHi0[15:0] = InHi[15:0];
  //   InHi16[15:0] = InHi[31:16]; InLo0[15:0] = InLo[15:0]; InLo16[15:0] = InLo[31:16]

  // Notes on the sheet:
  //   Vector Output Machine
  //   Bit Expand DSel4
  //   Mask
endmodule

module VALU (
  input  [31:0] AHi,
  input  [31:0] ALo,
  input  [2:0] op,
  input  [31:0] BHi,
  input  [31:0] BLo,
  output [31:0] ResHi,
  output [31:0] ResLo
);

  ALU16 alu16_1 (.arg0(BHi[31:16]), .arg0_2(AHi[31:16]), .opSel(op), .out_4(ResHi[31:16]));
  ALU16 alu16_2 (.arg0(BHi[15:0]), .arg0_2(AHi[15:0]), .opSel(op), .out_4(ResHi[15:0]));
  ALU16 alu16_3 (.arg0(BLo[31:16]), .arg0_2(ALo[31:16]), .opSel(op), .out_4(ResLo[31:16]));
  ALU16 alu16_4 (.arg0(BLo[15:0]), .arg0_2(ALo[15:0]), .opSel(op), .out_4(ResLo[15:0]));

  // Other names for the same wires on the sheet: AHi0[15:0] = AHi[15:0]; AHi16[15:0] = AHi[31:16];
  //   ALo0[15:0] = ALo[15:0]; ALo16[15:0] = ALo[31:16]; BHi0[15:0] = BHi[15:0]; BHi16[15:0] = BHi[31:16];
  //   BLo0[15:0] = BLo[15:0]; BLo16[15:0] = BLo[31:16]; opSel[2:0] = op
endmodule

module ALU16 (
  input  [15:0] arg0,
  input  [15:0] arg0_2,
  input  [2:0] opSel,
  output [15:0] out_4
);

  wire [15:0] adder_1_out, bit_extender_1_out, bit_extender_2_out, bit_extender_3_out, bit_extender_4_out,
       divider_1_out, multiplier_1_out, subtractor_1_out;

  Adder #(.width(16)) adder_1 (.a(arg0), .b(arg0_2), .out(adder_1_out));  // open: cin, cout
  Subtractor #(.width(16)) subtractor_1 (.a(arg0), .b(arg0_2), .out(subtractor_1_out));  // open: bin, bout
  Multiplier #(.width(16)) multiplier_1 (.a(arg0), .b(arg0_2), .out(multiplier_1_out));  // open: cin, cout
  Divider #(.width(16)) divider_1 (.a(arg0), .b(arg0_2), .out(divider_1_out));  // open: upper, rem
  assign bit_extender_1_out = {{8{1'b0}}, arg0[7:0]};  // Bit_Extender bit_extender_1
  assign bit_extender_2_out = {{8{1'b0}}, arg0[15:8]};  // Bit_Extender bit_extender_2
  assign bit_extender_3_out = {{8{arg0[7]}}, arg0[7:0]};  // Bit_Extender bit_extender_3
  assign bit_extender_4_out = {{8{1'b0}}, arg0[7:0]};  // Bit_Extender bit_extender_4
  Multiplexer #(.select(3), .width(16), .enable("false")) multiplexer_1 (
    .in0(adder_1_out), .in1(subtractor_1_out), .in2(multiplier_1_out), .in3(divider_1_out),
    .in4(bit_extender_1_out), .in5(bit_extender_2_out), .in6(bit_extender_3_out), .in7(bit_extender_4_out),
    .out(out_4), .sel(opSel));

  // Other names for the same wires on the sheet: arg1[15:0] = arg0_2
endmodule

module Pack (
  input  [31:0] InHi,
  input  [31:0] InLo,
  output [31:0] OutHi
);


  assign OutHi = {InHi[23:16], InHi[7:0], InLo[23:16], InLo[7:0]};
endmodule

module UnPack (
  input  [31:0] In,
  output [31:0] OutHi,
  output [31:0] OutLo
);


  assign OutHi = {{8{1'b0}}, In[31:24], {8{1'b0}}, In[23:16]};
  assign OutLo = {{8{1'b0}}, In[15:8], {8{1'b0}}, In[7:0]};
endmodule
